// Logisim project StickyStacky16.circ as structural Verilog: 1 circuit, main circuit main
module main (
  input  [15:0] Input,
  input  [1:0] SPsel,
  input  [1:0] Wsel,
  input  Clock
);

  wire and_5_out, not_1_out, not_2_out, or_1_out, sp_nop, sp_pop, sp_push, sp_reset;

  not not_1 (not_1_out, SPsel[0]);
  not not_2 (not_2_out, SPsel[1]);
  and and_1 (sp_push, SPsel[1], SPsel[0]);
  Register #(.width(16)) register_1 (.clk(Clock));  // open: D, en, Q, clr
  and and_2 (sp_nop, SPsel[1], not_1_out);
  Register #(.width(16)) register_2 (.clk(Clock));  // open: D, en, Q, clr
  Register #(.width(16)) register_3 (.clk(Clock));  // open: D, en, Q, clr
  and and_3 (sp_pop, not_2_out, SPsel[0]);
  and and_4 (sp_reset, not_2_out, not_1_out);
  Register #(.width(16)) register_4 (.clk(Clock));  // open: D, en, Q, clr
  Register #(.width(16)) register_5 (.clk(Clock));  // open: D, en, Q, clr
  Register #(.width(16)) register_6 (.clk(Clock));  // open: D, en, Q, clr
  Register #(.width(16)) register_7 (.clk(Clock));  // open: D, en, Q, clr
  Counter #(.width(4), .max('hf)) SP (
    .load(sp_push), .count(or_1_out), .clk(Clock), .clr(and_5_out));  // open: D, Q, carry
  or or_1 (or_1_out, sp_push, sp_pop);
  and and_5 (and_5_out, Clock, sp_reset);
  Register #(.width(16)) register_8 (.clk(Clock));  // open: D, en, Q, clr
  Register #(.width(16)) register_9 (.clk(Clock));  // open: D, en, Q, clr
  Register #(.width(16)) register_10 (.clk(Clock));  // open: D, en, Q, clr
  Register #(.width(16)) register_11 (.clk(Clock));  // open: D, en, Q, clr
  Register #(.width(16)) register_12 (.clk(Clock));  // open: D, en, Q, clr
  Register #(.width(16)) register_13 (.clk(Clock));  // open: D, en, Q, clr
  Register #(.width(16)) register_14 (.clk(Clock));  // open: D, en, Q, clr
  Register #(.width(16)) register_15 (.clk(Clock));  // open: D, en, Q, clr
  Register #(.width(16)) register_16 (.clk(Clock));  // open: D, en, Q, clr

  // Other names for the same wires on the sheet: spcell[1:0] = SPsel
endmodule
